// Logisim project Logisim Schematic.circ as structural Verilog: 1 circuit, main circuit main
module main (
);

  wire and_1_out, and_2_out, and_3_out, and_4_out, and_5_out, button_1_out, button_2_out, button_3_out,
       clock_1_out, j_k_ff_1_q, j_k_ff_2_q, j_k_ff_2_qn, n7447_1_pin3, n7447_1_pin9, n7447_1_pin10,
       n7447_1_pin11, n7447_1_pin12, n7447_1_pin13, n7447_1_pin14, n7447_1_pin15, n7447_2_pin3, n7447_2_pin9,
       n7447_2_pin10, n7447_2_pin11, n7447_2_pin12, n7447_2_pin13, n7447_2_pin14, n7447_2_pin15,
       n7447_3_pin3, n7447_3_pin9, n7447_3_pin10, n7447_3_pin11, n7447_3_pin12, n7447_3_pin13, n7447_3_pin14,
       n7447_3_pin15, n7447_4_pin3, n7447_4_pin9, n7447_4_pin10, n7447_4_pin11, n7447_4_pin12, n7447_4_pin13,
       n7447_4_pin14, n7447_4_pin15, n7447_5_pin3, n7447_5_pin9, n7447_5_pin10, n7447_5_pin11, n7447_5_pin12,
       n7447_5_pin13, n7447_5_pin14, n7447_5_pin15, n7447_6_pin3, n7447_6_pin9, n7447_6_pin10, n7447_6_pin11,
       n7447_6_pin12, n7447_6_pin13, n7447_6_pin14, n7447_6_pin15, n7447_7_pin3, n7447_7_pin9, n7447_7_pin10,
       n7447_7_pin11, n7447_7_pin12, n7447_7_pin13, n7447_7_pin14, n7447_7_pin15, n7447_8_pin3, n7447_8_pin9,
       n7447_8_pin10, n7447_8_pin11, n7447_8_pin12, n7447_8_pin13, n7447_8_pin14, n7447_8_pin15, or_1_out,
       or_2_out, or_3_out, or_4_out;
  wire [3:0] counter_1_q, counter_2_q, counter_3_q, counter_4_q;
  wire [7:0] register_1_q, register_2_q;

  Button button_1 (.out(button_1_out));
  J_K_Flip_Flop j_k_ff_1 (
    .J(1'b1), .K(1'b1), .clk(and_2_out), .Q(j_k_ff_1_q), .reset(button_2_out));  // open: Qn, preset
  LED led_1 (.in(j_k_ff_1_q));
  J_K_Flip_Flop j_k_ff_2 (
    .J(1'b1), .K(1'b1), .clk(button_1_out), .Q(j_k_ff_2_q), .Qn(j_k_ff_2_qn));  // open: preset, reset
  LED led_2 (.in(j_k_ff_2_q));
  Clock clock_1 (.out(clock_1_out));
  Button button_2 (.out(button_2_out));
  and and_1 (and_1_out, j_k_ff_2_qn, clock_1_out);
  Button button_3 (.out(button_3_out));
  Counter #(.max('hf), .width(4)) counter_1 (
    .clr(or_1_out), .load(1'b0), .up(1'b1), .count(and_3_out), .clk(and_3_out), .Q(counter_1_q));  // open: D, carry
  or or_1 (or_1_out, button_2_out, and_2_out);
  Counter #(.max('hf), .width(4)) counter_2 (
    .clr(or_2_out), .load(1'b0), .up(1'b1), .count(and_4_out), .clk(and_4_out), .Q(counter_2_q));  // open: D, carry
  or or_2 (or_2_out, button_2_out, and_3_out);
  Counter #(.max('hf), .width(4)) counter_3 (
    .clr(or_3_out), .load(1'b0), .up(1'b1), .count(and_5_out), .clk(and_5_out), .Q(counter_3_q));  // open: D, carry
  or or_3 (or_3_out, button_2_out, and_4_out);
  Counter #(.max('hf), .width(4)) counter_4 (
    .clr(or_4_out), .load(1'b0), .up(1'b1), .count(1'b1), .clk(and_1_out), .Q(counter_4_q));  // open: D, carry
  or or_4 (or_4_out, button_2_out, and_5_out);
  and and_2 (and_2_out, counter_1_q[2], counter_1_q[1], counter_1_q[0]);
  and and_3 (and_3_out, counter_2_q[1], counter_2_q[3]);
  and and_4 (and_4_out, counter_3_q[1], counter_3_q[3]);
  and and_5 (and_5_out, counter_4_q[1], counter_4_q[3]);
  _7447 u_7447_1 (
    .pin1(counter_1_q[1]), .pin2(counter_1_q[2]), .pin3(n7447_1_pin3), .pin4(n7447_1_pin3),
    .pin5(n7447_1_pin3), .pin6(counter_1_q[3]), .pin7(counter_1_q[0]), .pin15(n7447_1_pin15),
    .pin14(n7447_1_pin14), .pin13(n7447_1_pin13), .pin12(n7447_1_pin12), .pin11(n7447_1_pin11),
    .pin10(n7447_1_pin10), .pin9(n7447_1_pin9));
  _7447 u_7447_2 (
    .pin1(counter_2_q[1]), .pin2(counter_2_q[2]), .pin3(n7447_2_pin3), .pin4(n7447_2_pin3),
    .pin5(n7447_2_pin3), .pin6(counter_2_q[3]), .pin7(counter_2_q[0]), .pin15(n7447_2_pin15),
    .pin14(n7447_2_pin14), .pin13(n7447_2_pin13), .pin12(n7447_2_pin12), .pin11(n7447_2_pin11),
    .pin10(n7447_2_pin10), .pin9(n7447_2_pin9));
  _7447 u_7447_3 (
    .pin1(counter_3_q[1]), .pin2(counter_3_q[2]), .pin3(n7447_3_pin3), .pin4(n7447_3_pin3),
    .pin5(n7447_3_pin3), .pin6(counter_3_q[3]), .pin7(counter_3_q[0]), .pin15(n7447_3_pin15),
    .pin14(n7447_3_pin14), .pin13(n7447_3_pin13), .pin12(n7447_3_pin12), .pin11(n7447_3_pin11),
    .pin10(n7447_3_pin10), .pin9(n7447_3_pin9));
  _7447 u_7447_4 (
    .pin1(counter_4_q[1]), .pin2(counter_4_q[2]), .pin3(n7447_4_pin3), .pin4(n7447_4_pin3),
    .pin5(n7447_4_pin3), .pin6(counter_4_q[3]), .pin7(counter_4_q[0]), .pin15(n7447_4_pin15),
    .pin14(n7447_4_pin14), .pin13(n7447_4_pin13), .pin12(n7447_4_pin12), .pin11(n7447_4_pin11),
    .pin10(n7447_4_pin10), .pin9(n7447_4_pin9));
  _7_Segment_Display #(.active("false")) u_7_segment_display_1 (
    .g(n7447_1_pin14), .f(n7447_1_pin15), .a(n7447_1_pin13), .b(n7447_1_pin12), .e(n7447_1_pin9),
    .d(n7447_1_pin10), .c(n7447_1_pin11), .dp(1'b1));
  _7_Segment_Display #(.active("false")) u_7_segment_display_2 (
    .g(n7447_2_pin14), .f(n7447_2_pin15), .a(n7447_2_pin13), .b(n7447_2_pin12), .e(n7447_2_pin9),
    .d(n7447_2_pin10), .c(n7447_2_pin11), .dp(1'b0));
  _7_Segment_Display #(.active("false")) u_7_segment_display_3 (
    .g(n7447_3_pin14), .f(n7447_3_pin15), .a(n7447_3_pin13), .b(n7447_3_pin12), .e(n7447_3_pin9),
    .d(n7447_3_pin10), .c(n7447_3_pin11), .dp(1'b1));
  _7_Segment_Display #(.active("false")) u_7_segment_display_4 (
    .g(n7447_4_pin14), .f(n7447_4_pin15), .a(n7447_4_pin13), .b(n7447_4_pin12), .e(n7447_4_pin9),
    .d(n7447_4_pin10), .c(n7447_4_pin11), .dp(1'b1));
  Register register_1 (
    .D({counter_2_q, counter_1_q}), .en(button_3_out), .clk(button_3_out), .Q(register_1_q),
    .clr(button_2_out));
  Register register_2 (
    .D({counter_4_q, counter_3_q}), .en(button_3_out), .clk(button_3_out), .Q(register_2_q),
    .clr(button_2_out));
  _7447 u_7447_5 (
    .pin1(register_1_q[1]), .pin2(register_1_q[2]), .pin3(n7447_5_pin3), .pin4(n7447_5_pin3),
    .pin5(n7447_5_pin3), .pin6(register_1_q[3]), .pin7(register_1_q[0]), .pin15(n7447_5_pin15),
    .pin14(n7447_5_pin14), .pin13(n7447_5_pin13), .pin12(n7447_5_pin12), .pin11(n7447_5_pin11),
    .pin10(n7447_5_pin10), .pin9(n7447_5_pin9));
  _7447 u_7447_6 (
    .pin1(register_1_q[5]), .pin2(register_1_q[6]), .pin3(n7447_6_pin3), .pin4(n7447_6_pin3),
    .pin5(n7447_6_pin3), .pin6(register_1_q[7]), .pin7(register_1_q[4]), .pin15(n7447_6_pin15),
    .pin14(n7447_6_pin14), .pin13(n7447_6_pin13), .pin12(n7447_6_pin12), .pin11(n7447_6_pin11),
    .pin10(n7447_6_pin10), .pin9(n7447_6_pin9));
  _7447 u_7447_7 (
    .pin1(register_2_q[1]), .pin2(register_2_q[2]), .pin3(n7447_7_pin3), .pin4(n7447_7_pin3),
    .pin5(n7447_7_pin3), .pin6(register_2_q[3]), .pin7(register_2_q[0]), .pin15(n7447_7_pin15),
    .pin14(n7447_7_pin14), .pin13(n7447_7_pin13), .pin12(n7447_7_pin12), .pin11(n7447_7_pin11),
    .pin10(n7447_7_pin10), .pin9(n7447_7_pin9));
  _7447 u_7447_8 (
    .pin1(register_2_q[5]), .pin2(register_2_q[6]), .pin3(n7447_8_pin3), .pin4(n7447_8_pin3),
    .pin5(n7447_8_pin3), .pin6(register_2_q[7]), .pin7(register_2_q[4]), .pin15(n7447_8_pin15),
    .pin14(n7447_8_pin14), .pin13(n7447_8_pin13), .pin12(n7447_8_pin12), .pin11(n7447_8_pin11),
    .pin10(n7447_8_pin10), .pin9(n7447_8_pin9));
  _7_Segment_Display #(.active("false")) u_7_segment_display_5 (
    .g(n7447_5_pin14), .f(n7447_5_pin15), .a(n7447_5_pin13), .b(n7447_5_pin12), .e(n7447_5_pin9),
    .d(n7447_5_pin10), .c(n7447_5_pin11), .dp(1'b1));
  _7_Segment_Display #(.active("false")) u_7_segment_display_6 (
    .g(n7447_6_pin14), .f(n7447_6_pin15), .a(n7447_6_pin13), .b(n7447_6_pin12), .e(n7447_6_pin9),
    .d(n7447_6_pin10), .c(n7447_6_pin11), .dp(1'b0));
  _7_Segment_Display #(.active("false")) u_7_segment_display_7 (
    .g(n7447_7_pin14), .f(n7447_7_pin15), .a(n7447_7_pin13), .b(n7447_7_pin12), .e(n7447_7_pin9),
    .d(n7447_7_pin10), .c(n7447_7_pin11), .dp(1'b1));
  _7_Segment_Display #(.active("false")) u_7_segment_display_8 (
    .g(n7447_8_pin14), .f(n7447_8_pin15), .a(n7447_8_pin13), .b(n7447_8_pin12), .e(n7447_8_pin9),
    .d(n7447_8_pin10), .c(n7447_8_pin11), .dp(1'b0));
  // also tied to VCC on the sheet: {n7447_1_pin3, n7447_2_pin3, n7447_3_pin3, n7447_4_pin3, n7447_5_pin3, n7447_6_pin3, n7447_7_pin3, n7447_8_pin3}

  // Notes on the sheet:
  //   START/STOP
  //   OVERFLOW
  //   RESET
  //   CLOCK
  //   LAP
endmodule
